// Logisim project AdderCircuit.circ as structural Verilog: 2 circuits, main circuit Adder1bit
module Adder1bit (
  input  A,
  input  B,
  input  Cin,
  output S,
  output Cout
);

  wire and_1_out, and_2_out, xor_1_out;

  xor xor_1 (xor_1_out, A, B);
  and and_1 (and_1_out, B, A);
  and and_2 (and_2_out, xor_1_out, Cin);
  xor xor_2 (S, xor_1_out, Cin);
  or or_1 (Cout, and_2_out, and_1_out);
endmodule

module Adder4bit (
  input  [3:0] A_4bit,
  input  [3:0] B_4bit,
  input  Cin,
  output Cout,
  output [3:0] S_4bit
);

  wire adder1bit_2_cout, adder1bit_3_cout, adder1bit_4_cout;

  Adder1bit adder1bit_1 (.A(A_4bit[3]), .B(B_4bit[3]), .Cin(adder1bit_2_cout), .S(S_4bit[3]), .Cout(Cout));
  Adder1bit adder1bit_2 (.A(A_4bit[2]), .B(B_4bit[2]), .Cin(adder1bit_3_cout), .S(S_4bit[2]), .Cout(adder1bit_2_cout));
  Adder1bit adder1bit_3 (.A(A_4bit[1]), .B(B_4bit[1]), .Cin(adder1bit_4_cout), .S(S_4bit[1]), .Cout(adder1bit_3_cout));
  Adder1bit adder1bit_4 (.A(A_4bit[0]), .B(B_4bit[0]), .Cin(Cin), .S(S_4bit[0]), .Cout(adder1bit_4_cout));
endmodule
