// Logisim project NMOS.circ as structural Verilog: 4 circuits, main circuit NOT_GATE
module main (
  input  in_1,
  output Q,
  output Q_NOT
);

  wire clock_1_out, nand_gate_1_o, nand_gate_2_o, not_gate_1_o;

  Clock clock_1 (.out(clock_1_out));
  NOT_GATE not_gate_1 (.I(in_1), .O(not_gate_1_o));
  NAND_GATE nand_gate_1 (.A(in_1), .B(clock_1_out), .O(nand_gate_1_o));
  NAND_GATE nand_gate_2 (.A(clock_1_out), .B(not_gate_1_o), .O(nand_gate_2_o));
  NAND_GATE nand_gate_3 (.A(nand_gate_1_o), .B(Q_NOT), .O(Q));
  NAND_GATE nand_gate_4 (.A(Q), .B(nand_gate_2_o), .O(Q_NOT));
endmodule

module NOT_GATE (
  input  I,
  output O
);

  Transistor #(.\type ("n")) transistor_1 (.in(1'b0), .out(O), .gate(I));
  Pull_Resistor #(.pull(1)) pull_resistor_1 (.node(O));
endmodule

module NAND_GATE (
  input  A,
  input  B,
  output O
);

  wire transistor_2_out;

  Pull_Resistor #(.pull(1)) pull_resistor_1 (.node(O));
  Transistor #(.\type ("n")) transistor_1 (.in(transistor_2_out), .out(O), .gate(A));
  Transistor #(.\type ("n")) transistor_2 (.in(1'b0), .out(transistor_2_out), .gate(B));
endmodule

module NOR_GATE (
  input  A,
  input  B,
  output O
);

  Pull_Resistor #(.pull(1)) pull_resistor_1 (.node(O));
  Transistor #(.\type ("n")) transistor_1 (.in(1'b0), .out(O), .gate(A));
  Transistor #(.\type ("n")) transistor_2 (.in(1'b0), .out(O), .gate(B));
endmodule
