// Logisim project Lab3.circ as structural Verilog: 5 circuits, main circuit Adder4bt
module Adder4bt (
  input  [3:0] A,
  input  [3:0] B,
  input  Sel,
  output CF,
  output [3:0] R
);

  wire xor_1_out, xor_2_out, xor_3_out, xor_4_out;

  xor xor_1 (xor_1_out, B[3], Sel);
  Adder1bt adder1bt_1 (.A(A[3]), .B(xor_1_out), .S(R[3]), .Co(CF));  // open: Cin
  Adder1bt adder1bt_2 (.A(A[2]), .B(xor_2_out), .S(R[2]));  // open: Cin, Co
  xor xor_2 (xor_2_out, B[2], Sel);
  xor xor_3 (xor_3_out, B[1], Sel);
  Adder1bt adder1bt_3 (.A(A[1]), .B(xor_3_out), .S(R[1]));  // open: Cin, Co
  xor xor_4 (xor_4_out, B[0], Sel);
  Adder1bt adder1bt_4 (.A(A[0]), .B(xor_4_out), .Cin(Sel), .S(R[0]));  // open: Co
endmodule

module Adder1bt (
  input  A,
  input  B,
  input  Cin,
  output S,
  output Co
);

  wire and_1_out, and_2_out, xor_1_out;

  xor xor_1 (xor_1_out, A, B);
  and and_1 (and_1_out, B, A);
  xor xor_2 (S, xor_1_out, Cin);
  and and_2 (and_2_out, xor_1_out, Cin);
  or or_1 (Co, and_2_out, and_1_out);
endmodule

module AND4bit (
  input  [3:0] A,
  input  [3:0] B,
  output [3:0] R
);

  and and_1 (R[3], A[3], B[3]);
  and and_2 (R[2], A[2], B[2]);
  and and_3 (R[1], A[1], B[1]);
  and and_4 (R[0], A[0], B[0]);
endmodule

module ALU (
  input  [3:0] A,
  input  [3:0] B,
  input  [1:0] Op,
  output [3:0] R,
  output CF
);

  wire [3:0] ADD, AND4, SHL;

  Adder4bt adder4bt_1 (.Sel(Op[0]), .B(B), .A(A), .CF(CF), .R(ADD));
  AND4bit and4bit_1 (.B(B), .A(A), .R(AND4));
  LeftShifer4bit leftshifer4bit_1 (.B(B), .A(A), .R(SHL));
  Multiplexer #(.select(2), .width(4)) multiplexer_1 (.in0(ADD), .in1(ADD), .in2(AND4), .in3(SHL), .out(R), .sel(Op));

  // Other names for the same wires on the sheet: Sel = Op[0]
endmodule

module LeftShifer4bit (
  input  [3:0] A,
  input  [3:0] B,
  output [3:0] R
);

  Multiplexer #(.select(2)) multiplexer_1 (.in0(A[3]), .in1(A[2]), .in2(A[1]), .in3(A[0]), .out(R[3]), .sel(B[1:0]));
  Multiplexer #(.select(2)) multiplexer_2 (.in0(A[2]), .in1(A[1]), .in2(A[0]), .in3(1'b0), .out(R[2]), .sel(B[1:0]));
  Multiplexer #(.select(2)) multiplexer_3 (.in0(A[1]), .in1(A[0]), .in2(1'b0), .in3(1'b0), .out(R[1]), .sel(B[1:0]));
  Multiplexer #(.select(2)) multiplexer_4 (.in0(A[0]), .in1(1'b0), .in2(1'b0), .in3(1'b0), .out(R[0]), .sel(B[1:0]));

  // Other names for the same wires on the sheet: Sel[1:0] = B[1:0]
endmodule
