// Logisim project Lab4.circ as structural Verilog: 6 circuits, main circuit RF1bit
module RF1bit (
  input  CLK,
  input  Din,
  input  Sel,
  output Dout
);

  wire multiplexer_1_out;

  Multiplexer multiplexer_1 (.in0(Dout), .in1(Din), .out(multiplexer_1_out), .sel(Sel));
  D_Flip_Flop d_ff_1 (.clk(CLK), .D(multiplexer_1_out), .Q(Dout));  // open: Qn, preset, reset
endmodule

module RF2bit (
  input  [1:0] Din,
  input  Sel,
  input  CLK,
  output [1:0] Dout
);

  RF1bit rf1bit_1 (.CLK(CLK), .Din(Din[0]), .Sel(Sel), .Dout(Dout[0]));
  RF1bit rf1bit_2 (.CLK(CLK), .Din(Din[1]), .Sel(Sel), .Dout(Dout[1]));
endmodule

module RFSet (
  input  [1:0] RA,
  input  [1:0] WRD,
  input  REG_EN,
  input  [1:0] WA,
  input  CLK,
  input  [1:0] RB,
  output [1:0] A,
  output [1:0] B
);

  wire decoder_1_out0, decoder_1_out1, decoder_1_out2;
  wire [1:0] rf2bit_1_dout, rf2bit_2_dout, rf2bit_3_dout;

  Decoder #(.select(2)) decoder_1 (
    .out0(decoder_1_out0), .out1(decoder_1_out1), .out2(decoder_1_out2), .sel(WA), .en(REG_EN));  // open: out3
  RF2bit rf2bit_1 (.Sel(decoder_1_out0), .CLK(CLK), .Din(WRD), .Dout(rf2bit_1_dout));
  RF2bit rf2bit_2 (.Sel(decoder_1_out1), .CLK(CLK), .Din(WRD), .Dout(rf2bit_2_dout));
  RF2bit rf2bit_3 (.Sel(decoder_1_out2), .CLK(CLK), .Din(WRD), .Dout(rf2bit_3_dout));
  Multiplexer #(.select(2), .width(2)) multiplexer_1 (
    .in0(rf2bit_1_dout), .in1(rf2bit_2_dout), .in2(rf2bit_3_dout), .out(A), .sel(RA));  // open: in3
  Multiplexer #(.select(2), .width(2)) multiplexer_2 (
    .in0(rf2bit_1_dout), .in1(rf2bit_2_dout), .in2(rf2bit_3_dout), .out(B), .sel(RB));  // open: in3
endmodule

module RAM1x1 (
  input  Read_Select_1,
  input  CLK,
  input  Write_Data,
  input  Write_Sel,
  input  Read_Select_2,
  output Read_Data_1,
  output Read_Data_2
);

  wire d_ff_1_q, multiplexer_1_out;

  D_Flip_Flop d_ff_1 (.clk(CLK), .D(multiplexer_1_out), .Q(d_ff_1_q));  // open: Qn, preset, reset
  Multiplexer multiplexer_1 (.in0(d_ff_1_q), .in1(Write_Data), .out(multiplexer_1_out), .sel(Write_Sel));
  and and_1 (Read_Data_1, Read_Select_1, d_ff_1_q);
  and and_2 (Read_Data_2, d_ff_1_q, Read_Select_2);
endmodule

module RAM1x2 (
  input  RS1,
  input  RS2,
  input  WS,
  input  [1:0] WD,
  input  CLK,
  output [1:0] RD1,
  output [1:0] RD2
);

  RAM1x1 ram1x1_1 (
    .CLK(CLK), .Write_Data(WD[1]), .Write_Sel(WS), .Read_Select_1(RS1), .Read_Select_2(RS2),
    .Read_Data_1(RD1[1]), .Read_Data_2(RD2[1]));
  RAM1x1 ram1x1_2 (
    .CLK(CLK), .Write_Data(WD[0]), .Write_Sel(WS), .Read_Select_1(RS1), .Read_Select_2(RS2),
    .Read_Data_1(RD1[0]), .Read_Data_2(RD2[0]));

  // Other names for the same wires on the sheet: R1_0 = RD1[0]; R1_1 = RD1[1]; R2_0 = RD2[0]; R2_1 = RD2[1]
endmodule

module RAM2x2 (
  input  RA1,
  input  WE,
  input  WA,
  input  CLK,
  input  [1:0] WD,
  output [1:0] RD1
);

  wire decoder_1_out0, decoder_1_out1, decoder_2_out0, decoder_2_out1;
  wire [1:0] ram1x2_1_rd1, ram1x2_2_rd1;

  Decoder decoder_1 (.out0(decoder_1_out0), .out1(decoder_1_out1), .sel(RA1));  // open: en
  Decoder decoder_2 (.out0(decoder_2_out0), .out1(decoder_2_out1), .sel(WA), .en(WE));
  RAM1x2 ram1x2_1 (
    .CLK(CLK), .RS1(decoder_1_out0), .WS(decoder_2_out0), .WD(WD), .RD1(ram1x2_1_rd1));  // open: RS2, RD2
  RAM1x2 ram1x2_2 (
    .CLK(CLK), .RS1(decoder_1_out1), .WS(decoder_2_out1), .WD(WD), .RD1(ram1x2_2_rd1));  // open: RS2, RD2
  assign RD1 = ram1x2_1_rd1 | ram1x2_2_rd1;  // OR_Gate or_1, 2 bits wide
endmodule
